# Fritzing sketch PreventCataclysmSystems (saved by Fritzing 0.9.3b)
breadboards: 1

parts:
  Raspberry_Pi1 = Raspberry Pi 2
  DHT1 = DHT11 Humitidy and Temperature Sensor
  R1 = Resistor [tolerance=±5% resistance=2.2 package="0603 [SMD]"]
  IC1 = MCP3008 8-channel 10-bit ADC [part_number=MCP3008]
  Componente1 = Soil Moisture Sensor

nets:
  3V3: Raspberry_Pi1.3v3, Raspberry_Pi1.3V3, DHT1.VDD, R1.Pin_0, IC1.no_name_yet#15, IC1.no_name_yet#16, Componente1.VCC
  N1: Raspberry_Pi1.GPIO4, DHT1.DATA, R1.Pin_1
  N2: Raspberry_Pi1.GPIO10, IC1.no_name_yet#11
  N3: Raspberry_Pi1.GPIO9, IC1.no_name_yet#12
  N4: Raspberry_Pi1.GPIO11, IC1.no_name_yet#13
  GND: Raspberry_Pi1.GND, DHT1.GND, IC1.no_name_yet#9, IC1.no_name_yet#14, Componente1.GND
  N5: Raspberry_Pi1.GPIO8, IC1.no_name_yet#10
  N6: IC1.no_name_yet#6, Componente1.SIG

custom parts:
  DHT11 Humitidy and Temperature Sensor: DHT11 Humidity and Temperature Sensor
